// Logisim project Controller.circ as structural Verilog: 5 circuits, main circuit Controller
module Controller (
  input  [5:0] Op,
  input  [5:0] Func,
  output GRF_write,
  output [1:0] GRF_select,
  output Memory_read,
  output Memory_write,
  output ALU_select,
  output EXT_signed,
  output [1:0] ALU_main,
  output [4:0] EXT_width,
  output beq,
  output GRF_writeAddrSelect
);

  wire andlogic_1_addu, andlogic_1_beq, andlogic_1_lui, andlogic_1_lw, andlogic_1_ori, andlogic_1_sll,
       andlogic_1_subu, andlogic_1_sw;

  AndLogic andlogic_1 (
    .OperationCode(Op), .Function(Func), .addu(andlogic_1_addu), .subu(andlogic_1_subu),
    .sll(andlogic_1_sll), .ori(andlogic_1_ori), .lw(andlogic_1_lw), .sw(andlogic_1_sw), .beq(andlogic_1_beq),
    .lui(andlogic_1_lui));
  OrLogic orlogic_1 (
    .addu(andlogic_1_addu), .subu(andlogic_1_subu), .sll(andlogic_1_sll), .ori(andlogic_1_ori),
    .lw(andlogic_1_lw), .sw(andlogic_1_sw), .beq(andlogic_1_beq), .lui(andlogic_1_lui),
    .GRF_write(GRF_write), .GRF_select(GRF_select), .Memory_read(Memory_read), .Memory_write(Memory_write),
    .ALU_select(ALU_select), .EXT_signed(EXT_signed), .ALU_main(ALU_main), .Shifter_width(EXT_width),
    .beq_2(beq), .GRF_writeAddrSelect(GRF_writeAddrSelect));

  // Notes on the sheet:
  //   EXT_width: pull=down
endmodule

module AndLogic (
  input  [5:0] OperationCode,
  input  [5:0] Function,
  output addu,
  output subu,
  output sll,
  output ori,
  output lw,
  output sw,
  output beq,
  output lui
);

  wire andlogic_operationcodedetector_1_special;

  AndLogic__OperationCodeDetector andlogic_operationcodedetector_1 (
    .I26(OperationCode[0]), .I27(OperationCode[1]), .I28(OperationCode[2]), .I29(OperationCode[3]),
    .I30(OperationCode[4]), .I31(OperationCode[5]), .special(andlogic_operationcodedetector_1_special),
    .ori(ori), .lw(lw), .sw(sw), .beq(beq), .lui(lui));
  AddLogic__FuncrionDetector addlogic_funcriondetector_1 (
    .I0(Function[0]), .I1(Function[1]), .I2(Function[2]), .I3(Function[3]), .I4(Function[4]),
    .I5(Function[5]), .special(andlogic_operationcodedetector_1_special), .addu(addu), .subu(subu), .sll(sll));
endmodule

module AndLogic__OperationCodeDetector (
  input  I26,
  input  I27,
  input  I28,
  input  I29,
  input  I30,
  input  I31,
  output ori,
  output lw,
  output sw,
  output beq,
  output lui,
  output special
);

  wire not_1_out, not_2_out, not_3_out, not_4_out, not_5_out, not_6_out, not_7_out;

  not not_1 (not_1_out, I28);
  not not_2 (not_2_out, I31);
  not not_3 (not_3_out, I27);
  not not_4 (not_4_out, I29);
  not not_5 (not_5_out, I28);
  not not_6 (not_6_out, I29);
  not not_7 (not_7_out, I31);
  and and_1 (special, not_1_out, not_2_out);
  and and_2 (ori, I26, not_3_out);
  and and_3 (lw, I27, not_4_out);
  and and_4 (sw, not_5_out, I29);
  and and_5 (beq, I28, not_6_out);
  and and_6 (lui, I27, not_7_out);
endmodule

module AddLogic__FuncrionDetector (
  input  special,
  input  I0,
  input  I1,
  input  I2,
  input  I3,
  input  I4,
  input  I5,
  output addu,
  output subu,
  output sll
);

  wire and_1_out, not_1_out, not_2_out;

  not not_1 (not_1_out, I1);
  not not_2 (not_2_out, I5);
  and and_1 (and_1_out, I0, not_1_out);
  and and_2 (addu, and_1_out, special);
  and and_3 (subu, I1, special);
  and and_4 (sll, not_2_out, special);
endmodule

module OrLogic (
  input  addu,
  input  subu,
  input  sll,
  input  ori,
  input  lw,
  input  sw,
  input  beq,
  input  lui,
  output GRF_write,
  output [1:0] GRF_select,
  output Memory_read,
  output Memory_write,
  output ALU_select,
  output EXT_signed,
  output [1:0] ALU_main,
  output [4:0] Shifter_width,
  output beq_2,
  output GRF_writeAddrSelect
);

  or or_1 (GRF_write, addu, subu, ori, lw, lui);
  buf or_2 (GRF_select[0], lui);  // OR_Gate
  buf or_3 (GRF_select[1], lw);  // OR_Gate
  buf or_4 (Memory_read, lw);  // OR_Gate
  buf or_5 (Memory_write, sw);  // OR_Gate
  or or_6 (ALU_select, ori, lw, sw);
  or or_7 (EXT_signed, lw, sw, beq, lui);
  or or_8 (ALU_main[0], subu, beq);
  buf or_9 (ALU_main[1], ori);  // OR_Gate
  buf or_10 (Shifter_width[1], beq);  // OR_Gate
  buf or_11 (Shifter_width[4], lui);  // OR_Gate
  or or_12 (GRF_writeAddrSelect, ori, lw, lui);

  assign beq_2 = beq;
  assign {Shifter_width[3:2], Shifter_width[0]} = 3'b000;

  // Notes on the sheet:
  //   Shifter_width: pull=down
endmodule
