// Logisim project IFU.circ as structural Verilog: 1 circuit, main circuit IFU
module IFU (
  input  beq,
  input  Clock,
  input  Reset,
  input  [31:0] Offset,
  output [31:0] Instruction
);

  wire [31:0] multiplexer_1_out, n32_bit_adder_1_s, n32_bit_adder_2_s, PC_q;

  Multiplexer #(.width(32), .enable("false")) multiplexer_1 (
    .in0(n32_bit_adder_1_s), .in1(n32_bit_adder_2_s), .out(multiplexer_1_out), .sel(beq));
  Register #(.width(32)) PC (.D(multiplexer_1_out), .Q(PC_q), .clk(Clock), .clr(Reset));  // open: en
  _32_bit_adder u_32_bit_adder_1 (.A(PC_q), .B(32'h4), .S(n32_bit_adder_1_s));  // open: Cin, Cout
  _32_bit_adder u_32_bit_adder_2 (.A(n32_bit_adder_1_s), .B(Offset), .S(n32_bit_adder_2_s));  // open: Cin, Cout
  ROM #(.addrWidth(5), .dataWidth(32)) rom_1 (.addr(PC_q[6:2]), .data(Instruction));  // open: sel
endmodule
